# Fritzing sketch nano_board (saved by Fritzing 0.9.9b)
circuit board: 4.83968cm x 4.8618cm
breadboards: 1

parts:
  NanoRight = female pin header, 15 pins [form="♀ (female)"]
  Joystick = female pin header, 5 pins [form="♀ (female)"]
  Buttons = female pin header, 5 pins [form="♀ (female)"]
  NanoLeft = female pin header, 15 pins [form="♀ (female)"]

nets:
  N1: NanoRight.pin7, Buttons.pin1
  N2: NanoRight.pin8, Buttons.pin2
  N3: NanoRight.pin9, Buttons.pin3
  N4: NanoRight.pin10, Buttons.pin4
  N5: NanoRight.pin12, Buttons.pin5
  N6: Joystick.pin1, NanoLeft.pin7
  N7: Joystick.pin2, NanoLeft.pin8
  N8: Joystick.pin3, NanoLeft.pin9
  N9: Joystick.pin4, NanoLeft.pin12
  N10: Joystick.pin5, NanoLeft.pin14

notes:
  GND
  +5V
  VRx
  VRy
  SW
  PB1
  PB2
  PB3
  PB4
  ElectronicComputing.com
  ECS-NANODEMOBRD-2
  D13(16)
  D1(1)
