# Fritzing sketch push_buttons_board (saved by Fritzing 0.9.9b)
circuit board: 3.81cm x 2.53644cm
breadboards: 1

parts:
  Buttons = female pin header, 5 pins [form="♀ (female)"]
  PB1 = female pin header, 2 pins [form="♀ (female)"]
  PB2 = female pin header, 2 pins [form="♀ (female)"]
  PB3 = female pin header, 2 pins [form="♀ (female)"]
  PB4 = female pin header, 2 pins [form="♀ (female)"]

nets:
  N1: Buttons.pin1, PB1.pin2
  N2: Buttons.pin2, PB2.pin2
  N3: Buttons.pin3, PB3.pin1
  N4: Buttons.pin4, PB4.pin1
  N5: Buttons.pin5, PB1.pin1, PB2.pin1, PB3.pin2, PB4.pin2

notes:
  GND
  PB4
  PB3
  PB2
  PB1
