# Fritzing sketch push_buttons_board_v2 (saved by Fritzing 0.9.9b)
circuit board: 4.85656cm x 4.57509cm
breadboards: 1

parts:
  S2 = SWITCH-MOMENTARY-2 [package=tactile-pth-12mm]
  S3 = SWITCH-MOMENTARY-2 [package=tactile-pth-12mm]
  PB1 = SWITCH-MOMENTARY-2 [package=tactile-pth-12mm]
  Buttons = female pin header, 5 pins [form="♀ (female)"]
  S1 = SWITCH-MOMENTARY-2 [package=tactile-pth-12mm]

nets:
  N1: S2.1, S3.2, PB1.1, Buttons.pin5, S1.2
  N2: S2.2, Buttons.pin2
  N3: S3.1, Buttons.pin3
  N4: PB1.2, Buttons.pin1
  N5: Buttons.pin4, S1.1

notes:
  GND
  PB4
  PB3
  PB2
  PB1
  ElectronicComputing.com
  ECS-PB4BRD-2
