# Fritzing sketch wiring_diagram (saved by Fritzing 0.9.9b)

parts:
  PB1 = Tactile Switch Buttons - 12mm Square [package=tactile-pth-12mm]
  PB4 = Tactile Switch Buttons - 12mm Square [package=tactile-pth-12mm]
  PB3 = Tactile Switch Buttons - 12mm Square [package=tactile-pth-12mm]
  PB2 = Tactile Switch Buttons - 12mm Square [package=tactile-pth-12mm]
  Part2 = Arduino Nano (Rev3.0)
  Joystick = mystery part, 5 pins [chip_label=Joystick]

nets:
  N1: PB1.1, PB1.3, Part2.D6
  N2: PB1.2, PB1.4, PB4.2, PB4.4, PB3.2, PB3.4, PB2.2, PB2.4, Part2.GND, Joystick.pin1
  N3: PB4.1, Part2.D3
  N4: PB3.1, Part2.D4
  N5: PB2.1, PB2.3, Part2.D5
  N6: Part2.5V, Joystick.pin2
  N7: Part2.A5, Joystick.pin3
  N8: Part2.A4, Joystick.pin4
  N9: Part2.A3, Joystick.pin5

custom parts:
  Tactile Switch Buttons - 12mm Square: Medium-sized clicky momentary switches are standard input "buttons" on electronic projects. These work best in a PCB but can be used on a solderless breadboard as shown in this tutorial. The pins are normally open (disconnected) and when the button is pressed they are momentarily closed. They come in a pack of 10, they're pretty handy so you'll want to keep them around. You can find an EAGLE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
